# Fritzing sketch BLEUART_Controller (saved by Fritzing 0.9.2b)
breadboards: 1

parts:
  Arduino_Leonardo = Arduino Leonardo (Rev3b)
  Push_Button = Pushbutton [package="[SMD]"]
  Adafruit_Bluefruit_LE_UART_Friend = UART BLEFriend [part_number=2479]

nets:
  N1: Arduino_Leonardo.D0/RX, Adafruit_Bluefruit_LE_UART_Friend.TX
  N2: Arduino_Leonardo.D1/TX, Adafruit_Bluefruit_LE_UART_Friend.RXD
  N3: Arduino_Leonardo.D5_PWM, Adafruit_Bluefruit_LE_UART_Friend.MODE
  5V: Arduino_Leonardo.5V, Adafruit_Bluefruit_LE_UART_Friend.VIN
  GND: Arduino_Leonardo.GND, Push_Button.Pin_3, Push_Button.Pin_4, Adafruit_Bluefruit_LE_UART_Friend.GND, Adafruit_Bluefruit_LE_UART_Friend.CTS
  N4: Push_Button.Pin_1, Push_Button.Pin_2, Adafruit_Bluefruit_LE_UART_Friend.DFU
